# Fritzing sketch pull up (saved by Fritzing 0.9.4)
breadboards: 1

parts:
  Part1 = Arduino Uno (Rev3)
  S1 = Pushbutton [package="[THT]"]
  LED1 = LED - 5mm [color="Green (565nm)" package="5 mm [THT]"]
  R1 = Resistor [tolerance=±5% resistance=220 package="2512 [SMD]"]
  R2 = Resistor [tolerance=±5% resistance=2k package="2512 [SMD]"]

nets:
  N1: Part1.D8, S1.Pin_1, S1.Pin_2, R2.Pin_0
  N2: Part1.GND, S1.Pin_3, S1.Pin_4, R1.Pin_0
  N3: Part1.D2, LED1.anode
  N4: Part1.5V, R2.Pin_1
  N5: LED1.cathode, R1.Pin_1
